// Logisim project taimoorq3.circ as structural Verilog: 1 circuit, main circuit main
module main (
  input  [2:0] A,
  input  [2:0] B,
  input  [5:0] OUT,
  input  [1:0] SEL
);

  wire [2:0] adder_1_out, multiplier_1_out, subtractor_1_out;
  wire [5:0] bit_extender_1_out, bit_extender_2_out, bit_extender_3_out, multiplexer_1_out;

  Multiplier #(.width(3)) multiplier_1 (.a(A), .b(B), .out(multiplier_1_out));  // open: cin, cout
  Adder #(.width(3)) adder_1 (.a(A), .b(B), .out(adder_1_out));  // open: cin, cout
  Subtractor #(.width(3)) subtractor_1 (.a(A), .b(B), .out(subtractor_1_out));  // open: bin, bout
  assign bit_extender_1_out = {{3{1'b0}}, subtractor_1_out};  // Bit_Extender bit_extender_1
  assign bit_extender_2_out = {{3{1'b0}}, multiplier_1_out};  // Bit_Extender bit_extender_2
  assign bit_extender_3_out = {{3{1'b0}}, adder_1_out};  // Bit_Extender bit_extender_3
  Multiplexer #(.select(2), .width(6)) multiplexer_1 (
    .in0(bit_extender_3_out), .in1(bit_extender_1_out), .in2(bit_extender_2_out), .out(multiplexer_1_out),
    .sel(SEL));  // open: in3, en
endmodule
